// Logisim project Logisim-124-239.circ as structural Verilog: 4 circuits, main circuit main
module main (
  input  [7:0] User_input,
  input  in_2,
  output [7:0] Feedback_key,
  output [7:0] Encrypted_data,
  output [7:0] Decrypted_data
);

  wire clock_1_out, clock_2_out, n8x1_mux_1_out_12, n8x1_mux_2_out_12, n8x1_mux_3_out_12, n8x1_mux_4_out_12,
       n8x1_mux_5_out_12, n8x1_mux_6_out_12, n8x1_mux_7_out_12, n8x1_mux_8_out_12;
  wire [7:0] n2x1_mux_1_out_4, shift_register_1_out;

  Clock clock_1 (.out(clock_1_out));
  Shift_Register #(.width(8), .length(1)) shift_register_1 (
    .in(n2x1_mux_1_out_4), .clk(clock_1_out), .out(shift_register_1_out));  // open: shift, load, clr, d0, q0
  _2x1_mux u_2x1_mux_1 (.I0(Feedback_key), .Select(in_2), .out_4(n2x1_mux_1_out_4), .I1(8'h18));
  Clock clock_2 (.out(clock_2_out));
  _8x1_mux u_8x1_mux_1 (
    .in_1(1'b0), .in_2(1'b1), .in_3(1'b1), .in_4(1'b1), .in_5(1'b1), .in_6(1'b0), .in_7(1'b0), .in_8(1'b0),
    .out_12(n8x1_mux_1_out_12), .S2(shift_register_1_out[7]), .S1(shift_register_1_out[0]),
    .S0(shift_register_1_out[1]));
  _8x1_mux u_8x1_mux_2 (
    .in_1(1'b0), .in_2(1'b1), .in_3(1'b1), .in_4(1'b1), .in_5(1'b1), .in_6(1'b0), .in_7(1'b0), .in_8(1'b0),
    .out_12(n8x1_mux_2_out_12), .S2(shift_register_1_out[0]), .S1(shift_register_1_out[1]),
    .S0(shift_register_1_out[2]));
  _8x1_mux u_8x1_mux_3 (
    .in_1(1'b0), .in_2(1'b1), .in_3(1'b1), .in_4(1'b1), .in_5(1'b1), .in_6(1'b0), .in_7(1'b0), .in_8(1'b0),
    .out_12(n8x1_mux_3_out_12), .S2(shift_register_1_out[1]), .S1(shift_register_1_out[2]),
    .S0(shift_register_1_out[3]));
  _8x1_mux u_8x1_mux_4 (
    .in_1(1'b0), .in_2(1'b1), .in_3(1'b1), .in_4(1'b1), .in_5(1'b1), .in_6(1'b0), .in_7(1'b0), .in_8(1'b0),
    .out_12(n8x1_mux_4_out_12), .S2(shift_register_1_out[2]), .S1(shift_register_1_out[3]),
    .S0(shift_register_1_out[4]));
  _8x1_mux u_8x1_mux_5 (
    .in_1(1'b0), .in_2(1'b1), .in_3(1'b1), .in_4(1'b1), .in_5(1'b1), .in_6(1'b0), .in_7(1'b0), .in_8(1'b0),
    .out_12(n8x1_mux_5_out_12), .S2(shift_register_1_out[3]), .S1(shift_register_1_out[4]),
    .S0(shift_register_1_out[5]));
  _8x1_mux u_8x1_mux_6 (
    .in_1(1'b0), .in_2(1'b1), .in_3(1'b1), .in_4(1'b1), .in_5(1'b1), .in_6(1'b0), .in_7(1'b0), .in_8(1'b0),
    .out_12(n8x1_mux_6_out_12), .S2(shift_register_1_out[4]), .S1(shift_register_1_out[5]),
    .S0(shift_register_1_out[6]));
  _8x1_mux u_8x1_mux_7 (
    .in_1(1'b0), .in_2(1'b1), .in_3(1'b1), .in_4(1'b1), .in_5(1'b1), .in_6(1'b0), .in_7(1'b0), .in_8(1'b0),
    .out_12(n8x1_mux_7_out_12), .S2(shift_register_1_out[5]), .S1(shift_register_1_out[6]),
    .S0(shift_register_1_out[7]));
  _8x1_mux u_8x1_mux_8 (
    .in_1(1'b0), .in_2(1'b1), .in_3(1'b1), .in_4(1'b1), .in_5(1'b1), .in_6(1'b0), .in_7(1'b0), .in_8(1'b0),
    .out_12(n8x1_mux_8_out_12), .S2(shift_register_1_out[6]), .S1(shift_register_1_out[7]),
    .S0(shift_register_1_out[0]));
  D_Flip_Flop d_ff_1 (
    .clk(clock_2_out), .D(n8x1_mux_1_out_12), .Q(Feedback_key[0]), .en(1'b1));  // open: Qn, preset, reset
  D_Flip_Flop d_ff_2 (
    .clk(clock_2_out), .D(n8x1_mux_2_out_12), .Q(Feedback_key[1]), .en(1'b1));  // open: Qn, preset, reset
  D_Flip_Flop d_ff_3 (
    .clk(clock_2_out), .D(n8x1_mux_3_out_12), .Q(Feedback_key[2]), .en(1'b1));  // open: Qn, preset, reset
  D_Flip_Flop d_ff_4 (
    .clk(clock_2_out), .D(n8x1_mux_4_out_12), .Q(Feedback_key[3]), .en(1'b1));  // open: Qn, preset, reset
  D_Flip_Flop d_ff_5 (
    .clk(clock_2_out), .D(n8x1_mux_5_out_12), .Q(Feedback_key[4]), .en(1'b1));  // open: Qn, preset, reset
  D_Flip_Flop d_ff_6 (
    .clk(clock_2_out), .D(n8x1_mux_6_out_12), .Q(Feedback_key[5]), .en(1'b1));  // open: Qn, preset, reset
  D_Flip_Flop d_ff_7 (
    .clk(clock_2_out), .D(n8x1_mux_7_out_12), .Q(Feedback_key[6]), .en(1'b1));  // open: Qn, preset, reset
  D_Flip_Flop d_ff_8 (
    .clk(clock_2_out), .D(n8x1_mux_8_out_12), .Q(Feedback_key[7]), .en(1'b1));  // open: Qn, preset, reset
  xor_circuit XOR (
    .User_Input(User_input), .in_2(Feedback_key[0]), .in_3(Feedback_key[1]), .in_4(Feedback_key[2]),
    .in_5(Feedback_key[3]), .in_6(Feedback_key[4]), .in_7(Feedback_key[5]), .in_8(Feedback_key[6]),
    .in_9(Feedback_key[7]), .out_10(Encrypted_data));
  xor_circuit XOR_2 (
    .User_Input(Encrypted_data), .in_2(Feedback_key[0]), .in_3(Feedback_key[1]), .in_4(Feedback_key[2]),
    .in_5(Feedback_key[3]), .in_6(Feedback_key[4]), .in_7(Feedback_key[5]), .in_8(Feedback_key[6]),
    .in_9(Feedback_key[7]), .out_10(Decrypted_data));

  // Notes on the sheet:
  //   Initial key
  //   2x1 mux
  //   0x1e = 00011110
  //   Shift register
  //   DATA ENCRYPTION USING XOR
  //   16CO124-16CO239
  //   8x1 mux
  //   8x1 mux
  //   8x1 mux
  //   8x1 mux
  //   8x1 mux
  //   8x1 mux
  //   8x1 mux
  //   8x1 mux
  //   Enable
endmodule

module _8x1_mux (
  input  in_1,
  input  in_2,
  input  in_3,
  input  in_4,
  input  in_5,
  input  in_6,
  input  in_7,
  input  in_8,
  input  S2,
  input  S1,
  input  S0,
  output out_12
);

  wire and_1_out, and_2_out, and_3_out, and_4_out, and_5_out, and_6_out, and_7_out, and_8_out, not_1_out,
       not_2_out, not_3_out;

  not not_1 (not_1_out, S2);
  not not_2 (not_2_out, S1);
  not not_3 (not_3_out, S0);
  and and_1 (and_1_out, in_1, not_1_out, not_2_out, not_3_out);
  and and_2 (and_2_out, in_2, not_1_out, not_2_out, S0);
  and and_3 (and_3_out, in_3, not_1_out, S1, not_3_out);
  and and_4 (and_4_out, in_4, not_1_out, S1, S0);
  and and_5 (and_5_out, in_5, S2, not_2_out, not_3_out);
  and and_6 (and_6_out, in_6, S2, not_2_out, S0);
  and and_7 (and_7_out, in_7, S2, S1, not_3_out);
  and and_8 (and_8_out, in_8, S0, S1, S2);
  or or_1 (out_12, and_1_out, and_2_out, and_3_out, and_4_out, and_5_out, and_6_out, and_7_out, and_8_out);
endmodule

module xor_circuit (
  input  [7:0] User_Input,
  input  in_2,
  input  in_3,
  input  in_4,
  input  in_5,
  input  in_6,
  input  in_7,
  input  in_8,
  input  in_9,
  output [7:0] out_10
);

  xor xor_1 (out_10[0], User_Input[0], in_2);
  xor xor_2 (out_10[1], User_Input[1], in_3);
  xor xor_3 (out_10[2], User_Input[2], in_4);
  xor xor_4 (out_10[3], User_Input[3], in_5);
  xor xor_5 (out_10[4], User_Input[4], in_6);
  xor xor_6 (out_10[5], User_Input[5], in_7);
  xor xor_7 (out_10[6], User_Input[6], in_8);
  xor xor_8 (out_10[7], User_Input[7], in_9);
endmodule

module _2x1_mux (
  input  [7:0] I0,
  input  [7:0] I1,
  input  Select,
  output [7:0] out_4
);

  wire [7:0] and_1_out, and_2_out, not_1_out;

  assign not_1_out = ~{8{Select}};  // NOT_Gate not_1, 8 bits wide
  assign and_1_out = I0 & not_1_out;  // AND_Gate and_1, 8 bits wide
  assign and_2_out = I1 & {8{Select}};  // AND_Gate and_2, 8 bits wide
  assign out_4 = and_1_out | and_2_out;  // OR_Gate or_1, 8 bits wide
endmodule
